# Fritzing sketch distanse_sensor_circuit (saved by Fritzing 1.0.4)
breadboards: 1

parts:
  Mod1 = KY-033 Line Tracking Sensor Module [package="Breakout board"]
  Part1 = Arduino Uno (Rev3)

nets:
  GND: Mod1.GND, Part1.GND
  N1: Mod1.OUT, Part1.D6_PWM
  VCC: Mod1.VCC, Part1.5V

custom parts:
  KY-033 Line Tracking Sensor Module: KY-033 line tracking sensor module. An infrared sensor used to detect opaque surfaces.
