# Fritzing sketch joystick_sensor_circuit (saved by Fritzing 1.0.4)
breadboards: 1

parts:
  ARDUINO = Arduino Uno (Rev3)
  LED1 = LED - 5mm [color="Red (633nm)" current=0.030A package="5 mm [THT]"]
  LED2 = LED - 5mm [color="Red (633nm)" current=0.030A package="5 mm [THT]"]
  LED3 = LED - 5mm [color="Red (633nm)" current=0.030A package="5 mm [THT]"]
  LED4 = LED - 5mm [color="Red (633nm)" current=0.030A package="5 mm [THT]"]
  JOYSTICK = Thumb Joystick
  R1 = Resistor [tolerance=±0.1% power=0.5W resistance=1k package=THT]
  R2 = Resistor [tolerance=±0.1% power=0.5W resistance=1k package=THT]
  R3 = Resistor [tolerance=±0.1% power=0.5W resistance=1k package=THT]
  R4 = Resistor [tolerance=±0.1% power=0.5W resistance=1k package=THT]

nets:
  N1: ARDUINO.A0, JOYSTICK.VERT
  N2: ARDUINO.A5/SCL, JOYSTICK.HORZ
  N3: ARDUINO.D8, R3.Pin_0
  N4: ARDUINO.D9_PWM, LED2.anode, R1.Pin_0, R1.Pin_1
  N5: ARDUINO.D10_PWM/SS, R2.Pin_0
  GND: ARDUINO.GND, LED1.cathode, LED2.cathode, LED3.cathode, LED4.cathode, JOYSTICK.GND
  N6: ARDUINO.D7, R4.Pin_0
  5V: ARDUINO.5V, JOYSTICK.VCC
  N7: LED1.anode, R3.Pin_1
  N8: LED3.anode, R4.Pin_1
  N9: LED4.anode, R2.Pin_1
